// Logisim project Decodificador.circ as structural Verilog: 1 circuit, main circuit Decodificador
module Decodificador (
  input  x1,
  input  x2,
  output y0,
  output y1,
  output y2,
  output y3
);

  wire not_1_out, not_2_out;

  not not_1 (not_1_out, x1);
  not not_2 (not_2_out, x2);
  and and_1 (y0, not_2_out, not_1_out);
  and and_2 (y1, x1, not_2_out);
  and and_3 (y2, not_1_out, x2);
  and and_4 (y3, x1, x2);

  // Notes on the sheet:
  //   DECODIFICADOR
  //   __ __
  //   x1 x2 = y0
  //   __
  //   x1 x2 = y1
  //   __
  //   x1 x2 = y2
  //   x1 x2 = y3
endmodule
