// Logisim project Multiplexor.circ as structural Verilog: 1 circuit, main circuit main
module main (
  input  in_1,
  input  in_2,
  input  in_3,
  input  in_4,
  input  c1,
  input  c2,
  output b
);

  wire a0_out, a1_out, a2_out, a3_out, and_1_out, and_2_out, and_3_out, and_4_out, not_1_out, not_2_out,
       not_3_out, not_4_out, not_5_out, not_6_out;

  not not_1 (not_1_out, in_1);
  not not_2 (not_2_out, in_2);
  not not_3 (not_3_out, in_3);
  not not_4 (not_4_out, in_4);
  or a0 (a0_out, in_1, not_1_out);
  or a1 (a1_out, in_2, not_2_out);
  or a2 (a2_out, in_3, not_3_out);
  or a3 (a3_out, in_4, not_4_out);
  not not_5 (not_5_out, c1);
  not not_6 (not_6_out, c2);
  and and_1 (and_1_out, a0_out, not_5_out, not_6_out);
  and and_2 (and_2_out, a1_out, not_5_out, c2);
  and and_3 (and_3_out, a2_out, not_6_out, c1);
  and and_4 (and_4_out, a3_out, c1, c2);
  or or_1 (b, and_1_out, and_2_out, and_3_out, and_4_out);

  // Notes on the sheet:
  //   in_4: pull=up
  //   in_1: pull=up
  //   in_3: pull=up
  //   in_2: pull=up
  //   Las entradas deben de estar siempre activas.
  //   Es por eso que se hace uso del
  //   Tercero excluido
  //   Esto no tendría porque estar para el multiplexor.
  //   Pero simula mejor esto :)
  //   Deben de estar activos
  //   MULTIPLEXOR
  //   __
  //   __
  //   __
  //   b = c1 c2 a0 + c1 c2 a1 + c1 c2 a2 + c1 c2 a3
  //   __
endmodule
