// Logisim project Sumador.circ as structural Verilog: 1 circuit, main circuit main
module main (
  input  cj1,
  input  aj,
  input  bj,
  output cj,
  output sj1
);

  wire and_1_out, and_2_out, and_3_out, and_4_out, and_5_out, and_6_out, not_1_out, not_2_out, not_3_out,
       not_4_out, or_1_out, or_2_out;

  not not_1 (not_1_out, aj);
  not not_2 (not_2_out, bj);
  and and_1 (and_1_out, bj, not_1_out);
  and and_2 (and_2_out, aj, not_2_out);
  and and_3 (and_3_out, bj, aj);
  or or_1 (or_1_out, bj, aj);
  or or_2 (or_2_out, and_1_out, and_2_out);
  not not_3 (not_3_out, or_2_out);
  not not_4 (not_4_out, cj1);
  and and_4 (and_4_out, or_1_out, cj1);
  and and_5 (and_5_out, cj1, not_3_out);
  and and_6 (and_6_out, or_2_out, not_4_out);
  or or_3 (cj, and_3_out, and_4_out);
  or or_4 (sj1, and_5_out, and_6_out);

  // Notes on the sheet:
  //   SUMADOR
  //   __
  //   __
  //   __
  //   __
  //   (((aj bj) + (aj bj))cj1) + (((aj bj) + (aj bj)))cj1) = sj1
  //   ((aj + bj) cj1) + (aj bj) = cj (Si hay por lo menos dos 1's)
  //   __
endmodule
